// Logisim project Computerception.circ as structural Verilog: 14 circuits, main circuit main
module main (
  input  [3:0] AdressA,
  input  [15:0] Data,
  input  [3:0] AdressB,
  input  Clock,
  input  Enable,
  input  Reset,
  input  [3:0] BitSelector,
  output [15:0] DataA,
  output [15:0] Output,
  output [15:0] DataB
);

  Registrador registrador_1 (
    .Clock(Clock), .Enable(Enable), .Reset(Reset), .AdressA(AdressA), .AdressB(AdressB), .Data(Data),
    .DataB(DataB), .DataA(DataA));
  ULA ula_1 (.in_1(DataA), .in_2(DataB), .Out(Output), .BitSelector(BitSelector), .Enable(Enable));
endmodule

module FullAdder (
  input  a,
  input  b,
  input  ci,
  output s,
  output co
);

  wire halfsum_1_c, halfsum_1_s, halfsum_2_c;

  HalfSum halfsum_1 (.a(a), .b(b), .s(halfsum_1_s), .c(halfsum_1_c));
  HalfSum halfsum_2 (.a(halfsum_1_s), .b(ci), .s(s), .c(halfsum_2_c));
  or or_1 (co, halfsum_2_c, halfsum_1_c);
endmodule

module HalfSum (
  input  a,
  input  b,
  output s,
  output c
);

  xor xor_1 (s, a, b);
  and and_1 (c, a, b);
endmodule

module _4_bit_Ripple_Carry_Adder (
  input  ci,
  input  b0,
  input  b1,
  input  b2,
  input  b3,
  input  a0,
  input  a1,
  input  a2,
  input  a3,
  output s0,
  output s1,
  output s2,
  output s3,
  output co
);

  wire fulladder_1_co, fulladder_2_co, fulladder_3_co;

  LED led_1 (.in(s0));
  FullAdder fulladder_1 (.a(a0), .b(b0), .ci(ci), .s(s0), .co(fulladder_1_co));
  LED led_2 (.in(s1));
  FullAdder fulladder_2 (.a(a1), .b(b1), .ci(fulladder_1_co), .s(s1), .co(fulladder_2_co));
  LED led_3 (.in(s2));
  FullAdder fulladder_3 (.a(a2), .b(b2), .ci(fulladder_2_co), .s(s2), .co(fulladder_3_co));
  FullAdder fulladder_4 (.a(a3), .b(b3), .ci(fulladder_3_co), .s(s3), .co(co));
  LED led_4 (.in(s3));
  LED led_5 (.in(co));

  // Notes on the sheet:
  //   1
  //   1
  //   1
  //   2
  //   4
  //   2
  //   4
  //   2
  //   8
  //   8
  //   4
  //   8
  //   16
endmodule

module _4_bit_wirh_splitter (
  input  [3:0] in_1,
  input  [3:0] in_2,
  input  in_3,
  output [4:0] out_4
);

  wire fulladder_2_co, fulladder_3_co, fulladder_4_co;

  FullAdder fulladder_1 (.a(in_2[3]), .b(in_1[3]), .ci(fulladder_3_co), .s(out_4[3]), .co(out_4[4]));
  FullAdder fulladder_2 (.a(in_2[1]), .b(in_1[1]), .ci(fulladder_4_co), .s(out_4[1]), .co(fulladder_2_co));
  FullAdder fulladder_3 (.a(in_2[2]), .b(in_1[2]), .ci(fulladder_2_co), .s(out_4[2]), .co(fulladder_3_co));
  FullAdder fulladder_4 (.a(in_2[0]), .b(in_1[0]), .ci(in_3), .s(out_4[0]), .co(fulladder_4_co));
endmodule

module _8_bit_adder (
  input  [7:0] in_1,
  input  [7:0] in_2,
  input  ci,
  output c0,
  output [7:0] out_5
);

  wire n4_bit_ripple_carry_adder_2_co;

  _4_bit_Ripple_Carry_Adder u_4_bit_ripple_carry_adder_1 (
    .ci(n4_bit_ripple_carry_adder_2_co), .b0(in_2[4]), .a0(in_1[4]), .b1(in_2[5]), .a1(in_1[5]),
    .b2(in_1[6]), .a2(in_2[6]), .b3(in_2[7]), .a3(in_1[7]), .s0(out_5[4]), .s1(out_5[5]), .s2(out_5[6]),
    .s3(out_5[7]), .co(c0));
  // Probe on in_1
  // Probe on in_2
  _4_bit_Ripple_Carry_Adder u_4_bit_ripple_carry_adder_2 (
    .ci(ci), .b0(in_2[0]), .a0(in_1[0]), .b1(in_2[1]), .a1(in_1[1]), .b2(in_2[2]), .a2(in_1[2]),
    .b3(in_2[3]), .a3(in_1[3]), .s0(out_5[0]), .s1(out_5[1]), .s2(out_5[2]), .s3(out_5[3]),
    .co(n4_bit_ripple_carry_adder_2_co));
  // Probe on out_5
endmodule

module _16_bit_adder (
  input  [15:0] in_1,
  input  [15:0] in_2,
  input  ci,
  output co,
  output [15:0] out_5
);

  wire n8_bit_adder_2_c0;

  // Probe on in_1
  _8_bit_adder u_8_bit_adder_1 (
    .in_1(in_2[15:8]), .in_2(in_1[15:8]), .c0(co), .ci(n8_bit_adder_2_c0), .out_5(out_5[15:8]));
  // Probe on out_5
  // Probe on in_2
  _8_bit_adder u_8_bit_adder_2 (
    .in_1(in_2[7:0]), .in_2(in_1[7:0]), .c0(n8_bit_adder_2_c0), .ci(ci), .out_5(out_5[7:0]));
endmodule

module _32_bit_adder (
  input  [31:0] in_1,
  input  [31:0] in_2,
  input  ci,
  output co,
  output [31:0] out_5
);

  wire n16_bit_adder_2_co;

  // Probe on in_1
  _16_bit_adder u_16_bit_adder_1 (
    .in_1(in_2[31:16]), .in_2(in_1[31:16]), .out_5(out_5[31:16]), .ci(n16_bit_adder_2_co), .co(co));
  // Probe on out_5
  _16_bit_adder u_16_bit_adder_2 (
    .in_1(in_2[15:0]), .in_2(in_1[15:0]), .out_5(out_5[15:0]), .ci(ci), .co(n16_bit_adder_2_co));
  // Probe on in_2
endmodule

module SR_Latch (
  input  S,
  input  R,
  output Q_prime
);

  wire and_1_out, and_2_out, not_2_out;

  and and_1 (and_1_out, S, not_2_out);
  not not_1 (Q_prime, and_1_out);
  not not_2 (not_2_out, and_2_out);
  and and_2 (and_2_out, Q_prime, R);
endmodule

module D_Latch (
  input  Data,
  input  Enable,
  output Q
);

  wire and_1_out, and_2_out, not_1_out, not_2_out, not_3_out;

  not not_1 (not_1_out, Data);
  and and_1 (and_1_out, Data, Enable);
  and and_2 (and_2_out, Enable, not_1_out);
  not not_2 (not_2_out, and_1_out);
  SR_Latch sr_latch_1 (.S(not_2_out), .R(not_3_out), .Q_prime(Q));
  not not_3 (not_3_out, and_2_out);
endmodule

module Aula2 (
  input  in_1,
  input  in_2,
  input  in_3,
  input  in_4,
  input  in_5,
  input  in_6,
  input  in_7,
  input  in_8,
  input  in_9,
  input  in_10,
  input  in_11,
  input  in_12,
  output out_13,
  output out_14,
  output out_15,
  output out_16,
  output out_17,
  output out_18,
  output out_19,
  output out_20,
  output out_21,
  output Q,
  output out_23,
  output Q_prime
);

  wire and_1_out, and_2_out, and_3_out, and_4_out, and_5_out, and_6_out, and_7_out, and_8_out, and_9_out,
       and_10_out, and_11_out, and_12_out, not_1_out, not_8_out, not_9_out, not_10_out, not_11_out,
       not_12_out, not_13_out, or_1_out, or_2_out, or_3_out, or_4_out, or_5_out, or_6_out;

  and and_1 (and_1_out, in_2, out_15);
  and and_2 (and_2_out, out_13, in_4);
  or or_1 (or_1_out, in_6, out_19);
  or or_2 (or_2_out, out_17, in_8);
  not not_1 (not_1_out, in_9);
  or or_3 (or_3_out, not_1_out, out_23);
  or or_4 (or_4_out, out_21, in_9);
  Clock clock_1 ();  // open: out
  not not_2 (out_13, and_1_out);
  not not_3 (out_15, and_2_out);
  not not_4 (out_17, or_1_out);
  not not_5 (out_19, or_2_out);
  not not_6 (out_21, or_3_out);
  not not_7 (out_23, or_4_out);
  not not_8 (not_8_out, in_1);
  not not_9 (not_9_out, in_5);
  not not_10 (not_10_out, and_3_out);
  and and_3 (and_3_out, in_1, in_3);
  not not_11 (not_11_out, and_4_out);
  and and_4 (and_4_out, in_3, not_8_out);
  and and_5 (and_5_out, in_5, in_7);
  and and_6 (and_6_out, in_7, not_9_out);
  and and_7 (and_7_out, Q_prime, in_10, in_11);
  not not_12 (not_12_out, and_7_out);
  not not_13 (not_13_out, and_8_out);
  and and_8 (and_8_out, in_11, in_12, Q);
  and and_9 (and_9_out, not_10_out, out_16);
  and and_10 (and_10_out, out_14, not_11_out);
  not not_14 (out_18, or_5_out);
  or or_5 (or_5_out, and_5_out, out_20);
  not not_15 (out_20, or_6_out);
  or or_6 (or_6_out, out_18, and_6_out);
  and and_11 (and_11_out, not_12_out, Q_prime);
  and and_12 (and_12_out, Q, not_13_out);
  not not_16 (out_14, and_9_out);
  not not_17 (out_16, and_10_out);
  not not_18 (Q, and_11_out);
  not not_19 (Q_prime, and_12_out);
endmodule

module SR_Flip_Flop (
  input  D,
  input  Enable,
  input  Clock,
  output Q
);

  wire and_1_out, d_latch_1_q, not_1_out;

  and and_1 (and_1_out, Enable, Clock);
  D_Latch d_latch_1 (.Data(D), .Enable(and_1_out), .Q(d_latch_1_q));
  not not_1 (not_1_out, Clock);
  D_Latch d_latch_2 (.Data(d_latch_1_q), .Enable(not_1_out), .Q(Q));
endmodule

module Registrador (
  input  Clock,
  input  Enable,
  input  Reset,
  input  [3:0] AdressA,
  input  [3:0] AdressB,
  input  [15:0] Data,
  output [15:0] DataA,
  output [15:0] DataB
);

  wire clk, clock_1_out, en0, en1, en2, en3, en4, en5, en6, en7, en8, en9, en10, en11, en12, en13, en14, en15;
  wire [15:0] out0, out1, out2, out3, out4, out5, out6, out7, out8, out9, out10, out11, out12, out13, out14,
       out15;

  Clock clock_1 (.out(clock_1_out));
  or or_1 (clk, clock_1_out, Clock);
  Register #(.width(16)) register_1 (.D(Data), .en(en0), .Q(out0), .clk(clk), .clr(Reset));
  Register #(.width(16)) register_2 (.D(Data), .en(en4), .Q(out4), .clk(clk), .clr(Reset));
  Register #(.width(16)) register_3 (.D(Data), .en(en8), .Q(out8), .clk(clk), .clr(Reset));
  Register #(.width(16)) register_4 (.D(Data), .en(en12), .Q(out12), .clk(clk), .clr(Reset));
  Demultiplexer #(.select(4)) demultiplexer_1 (
    .out0(en0), .out1(en1), .out2(en2), .out3(en3), .out4(en4), .out5(en5), .out6(en6), .out7(en7),
    .out8(en8), .out9(en9), .out10(en10), .out11(en11), .out12(en12), .out13(en13), .out14(en14),
    .out15(en15), .in(Enable), .sel(AdressA));  // open: en
  Register #(.width(16)) register_5 (.D(Data), .en(en1), .Q(out1), .clk(clk), .clr(Reset));
  Register #(.width(16)) register_6 (.D(Data), .en(en5), .Q(out5), .clk(clk), .clr(Reset));
  Register #(.width(16)) register_7 (.D(Data), .en(en9), .Q(out9), .clk(clk), .clr(Reset));
  Register #(.width(16)) register_8 (.D(Data), .en(en13), .Q(out13), .clk(clk), .clr(Reset));
  Register #(.width(16)) register_9 (.D(Data), .en(en2), .Q(out2), .clk(clk), .clr(Reset));
  Register #(.width(16)) register_10 (.D(Data), .en(en6), .Q(out6), .clk(clk), .clr(Reset));
  Register #(.width(16)) register_11 (.D(Data), .en(en10), .Q(out10), .clk(clk), .clr(Reset));
  Register #(.width(16)) register_12 (.D(Data), .en(en14), .Q(out14), .clk(clk), .clr(Reset));
  Multiplexer #(.select(4), .width(16)) multiplexer_1 (
    .in0(out0), .in1(out1), .in2(out2), .in3(out3), .in4(out4), .in5(out5), .in6(out6), .in7(out7),
    .in8(out8), .in9(out9), .in10(out10), .in11(out11), .in12(out12), .in13(out13), .in14(out14),
    .in15(out15), .out(DataA), .sel(AdressA));  // open: en
  Register #(.width(16)) register_13 (.D(Data), .en(en3), .Q(out3), .clk(clk), .clr(Reset));
  Register #(.width(16)) register_14 (.D(Data), .en(en7), .Q(out7), .clk(clk), .clr(Reset));
  Register #(.width(16)) register_15 (.D(Data), .en(en11), .Q(out11), .clk(clk), .clr(Reset));
  Register #(.width(16)) register_16 (.D(Data), .en(en15), .Q(out15), .clk(clk), .clr(Reset));
  Multiplexer #(.select(4), .width(16)) multiplexer_2 (
    .in0(out0), .in1(out1), .in2(out2), .in3(out3), .in4(out4), .in5(out5), .in6(out6), .in7(out7),
    .in8(out8), .in9(out9), .in10(out10), .in11(out11), .in12(out12), .in13(out13), .in14(out14),
    .in15(out15), .out(DataB), .sel(AdressB));  // open: en

  // Other names for the same wires on the sheet: rst = Reset
endmodule

module ULA (
  input  [15:0] in_1,
  input  [15:0] in_2,
  input  [3:0] BitSelector,
  input  Enable,
  output [15:0] Out
);

  wire [15:0] DivOut, MinusDivide, MinusOut, multiplier_3_out, MultOut, Squared, subtractor_1_out, SumOut,
       TimesSum;

  Multiplier #(.width(16)) multiplier_1 (.a(in_1), .b(in_2), .out(MultOut));  // open: cin, cout
  Adder #(.width(16)) adder_1 (.a(in_1), .b(in_2), .out(SumOut));  // open: cin, cout
  Divider #(.width(16)) divider_1 (.a(in_1), .b(in_2), .out(DivOut));  // open: upper, rem
  Multiplier #(.width(16)) multiplier_2 (.a(in_1), .b(in_1), .out(Squared));  // open: cin, cout
  Multiplier #(.width(16)) multiplier_3 (.a(in_1), .b(in_2), .out(multiplier_3_out));  // open: cin, cout
  Subtractor #(.width(16)) subtractor_1 (.a(in_1), .b(in_2), .out(subtractor_1_out));  // open: bin, bout
  Subtractor #(.width(16)) subtractor_2 (.a(in_1), .b(in_2), .out(MinusOut));  // open: bin, bout
  Adder #(.width(16)) adder_2 (.a(multiplier_3_out), .b(in_2), .out(TimesSum));  // open: cin, cout
  Divider #(.width(16)) divider_2 (.a(subtractor_1_out), .b(in_2), .out(MinusDivide));  // open: upper, rem
  Multiplexer #(.select(4), .width(16)) multiplexer_1 (
    .in1(TimesSum), .in4(MultOut), .in6(MinusOut), .in8(MinusDivide), .in10(DivOut), .in12(Squared),
    .in13(SumOut), .out(Out), .sel(BitSelector), .en(Enable));  // open: in0, in2, in3, in5, in7, in9, in11, in14, in15

  // Other names for the same wires on the sheet: a[15:0] = in_1; b[15:0] = in_2
endmodule
